# Fritzing sketch max9814 (saved by Fritzing 0.9.3b)
breadboards: 1

parts:
  Componente1 = Adafruit MAX9814 Electret Microphone Amplifier [part_number="Adafruit #1713"]
  Componente2 = Arduino Nano (Rev3.0)

nets:
  GND: Componente1.GND, Componente2.GND
  VDD: Componente1.VDD, Componente1.GAIN, Componente2.5V
  N1: Componente1.OUTPUT, Componente2.A0

notes:
  max9814 (2.7-5.5v)

custom parts:
  Adafruit MAX9814 Electret Microphone Amplifier: Add an ear to your project with this well-designed electret microphone amplifier with AGC. This fully assembled and tested board comes with a 20-20KHz electret microphone soldered on. For the amplification, we use the Maxim MAX9814, a specialty chip that is designed for amplifying electret microphones in situations where the loudness of the audio isn't predictable. This fancy microphone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
