# Fritzing sketch sw400 (saved by Fritzing 0.9.3b)
breadboards: 1

parts:
  Componente1 = Arduino Nano (Rev3.0)
  SW-1 = Vibration sensor module

nets:
  N1: Componente1.D3, SW-1.Digital_output
  N2: Componente1.GND, SW-1.Ground
  5V: Componente1.5V, SW-1.vcc

custom parts:
  Vibration sensor module: Single-roller type full induction trigger switch. When no vibration or tilt, the product is ON conduction state, and in the steady state, when a vibration or tilt, the switch will be rendered instantly disconnect the conductive resistance increases, generating a current pulse signal, thereby triggering circuit. The default state of the swith is close Digital output Supply voltage:3.3V-5V On-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
