# Fritzing sketch tcs34725 (saved by Fritzing 0.9.3b)
breadboards: 1

parts:
  Componente1 = Arduino Mega ADK (Rev3)
  R1 = Resistor [tolerance=±5% resistance=220 package=THT]
  R2 = Resistor [tolerance=±5% resistance=220 package=THT]
  LED1 = RGB LED (com. cathode, rgb) [package="5 mm [THT]"]
  R3 = Resistor [tolerance=±5% resistance=220 package=THT]
  Componente2 = Adafruit TCS34725 RGB Color Sensor [part_number="Adafruit #1334"]

nets:
  N1: Componente1.D21/SCL, Componente2.SCL
  N2: Componente1.D20/SDA, Componente2.SDA
  N3: Componente1.D4_PWM, R3.Pin_0
  N4: Componente1.D5_PWM, R2.Pin_0
  N5: Componente1.D6_PWM, R1.Pin_0
  N6: R1.Pin_1, LED1.red_anode
  N7: R2.Pin_1, LED1.green_anode
  N8: LED1.blue_anode, R3.Pin_1
  VIN: Componente2.VIN, Componente2.GND, Componente2.LED_EN

custom parts:
  Adafruit TCS34725 RGB Color Sensor: Your electronics can now see in dazzling color with this lovely color light sensor. We found the best color sensor on the market, the TCS34725, which has RGB and Clear light sensing elements. An IR blocking filter, integrated on-chip and localized to the color sensing photodiodes, minimizes the IR spectral component of the incoming light and allows color measurements to be made accurately. The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
